# Fritzing sketch wiring-diagram(fritzing) (saved by Fritzing 0.9.5d)

parts:
  A1 = DORHEA ESP32 GPIO breakout board 30pin
  U1 = ESP32S-HiLetgo [part_number=ESP32S-HiLetgo]  # not connected
  A2 = DHT22 module
  Part1 = HC-SR501 Body Sensor Module
  KF-1 = KF-301 Relay [package=THT]
  WATER_PUMP1 = water pump/motor  # not connected
  VCC1 = Battery
  Part2 = LCD1602-I2C

nets:
  GND: A1.Pin_31, A1.Pin_55, A1.Pin_56, A1.Pin_67, A1.Pin_81, A1.Pin_85, A1.Pin_101, A2.GND, Part1.GND, KF-1.ground, Part2.GND
  VCC: A1.Pin_59, A1.Pin_60, A2.VCC, Part1.VCC
  N1: A1.Pin_76, A1.Pin_83, Part2.SDA
  N2: A1.Pin_79, A1.Pin_84, Part2.SCL
  N3: A1.Pin_82, Part2.VCC
  N4: A1.Pin_86, KF-1.power
  N5: A1.Pin_115, A2.DAT
  N6: A1.Pin_117, Part1.OUT
  N7: A1.Pin_118, KF-1.signal
  N8: KF-1.NO, VCC1.+

notes:
  LCD I2C
  VCC - 3.3
  GND - GND
  SDA - D21
  SCL - D22
  Water Pump
  RED - COM
  BLACK - battery (-)
  Positive - NO
  Negative - Waterpump
  Relay
  VCC - 3.3
  GND - GND
  IN - D16
  DHT22
  DAT - D15
  VCC - 5V
  GND - GND
  PIR
  VNC - 5v
  GND - GND
  OUT - D4

custom parts:
  DORHEA ESP32 GPIO breakout board 30pin: ESP32 shield 30P expansion board, supports two power supply : DC 6.5-16v and USB 5.V
  ESP32S-HiLetgo: HiLetgo ESP-WROOM-32 ESP32 ESP-32S Development Board 2.4GHz Dual-Mode WiFi + Bluetooth Dual Cores Microcontroller The ESP32 integrated with Antenna switches, RF Balun, power amplifiers, low-noise amplifiers, filters, and management modules, and the entire solution occupies the least area of PCB. 2.4 GHz Wi-Fi plus Bluetooth dual-mode chip, with TSMC Ultra-low power consumption 40nm technology,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
  DHT22 module: DHT22 module. Pins GND VCC Data.
  HC-SR501 Body Sensor Module: Pyroelectric Infrared PIR Motion Sensor Detector Module
  KF-301 Relay: KF-301
  water pump/motor: WATER PUMP BY ARDUBLOCKTR
  Battery: Your standard 2x 18650 battery pack (7,4 Volts)
  LCD1602-I2C: A standard character display, usually with 2x16 characters. Comes in many colors with LCM1602 IIC attached.
